# Fritzing sketch moisture_schematics (saved by Fritzing 0.9.3b)
breadboards: 1

parts:
  Part1 = Arduino Mega 2560 (Rev3)
  LED1 = LED - 5mm [color="Red (633nm)" package="5 mm [THT]"]
  LED2 = LED - 5mm [color="Orange (620nm)" package="5 mm [THT]"]
  LED3 = LED - 5mm [color="Green (570nm)" package="5 mm [THT]"]
  R1 = Resistor [tolerance=±5% resistance=220 package=THT]
  R2 = Resistor [tolerance=±5% resistance=220 package=THT]
  R3 = Resistor [tolerance=±5% resistance=220 package=THT]
  Part2 = Soil Moisture Sensor
  hc-sr1 = hc-sr04

nets:
  N1: Part1.A0, Part2.SIG
  VCC: Part1.5V, Part2.VCC, hc-sr1.VCC
  GND: Part1.GND, R1.Pin_0, R2.Pin_0, R3.Pin_1, Part2.GND, hc-sr1.GND
  N2: Part1.D2_PWM, LED3.anode
  N3: Part1.D3_PWM, LED1.anode
  N4: Part1.D4_PWM, LED2.anode
  N5: Part1.D5_PWM, hc-sr1.Trig
  N6: Part1.D6_PWM, hc-sr1.Echo
  N7: LED1.cathode, R3.Pin_0
  N8: LED2.cathode, R2.Pin_1
  N9: LED3.cathode, R1.Pin_1
